# Fritzing sketch reading light (saved by Fritzing 0.9.2b)
breadboards: 1

parts:
  Part1 = Arduino Nano (Rev3.0)
  RE1 = Rotary Encoder [package=THT]
  Part2 = 16 NeoPixel Ring [part_number=1463]
  PIR1 = PIR sensor
  R1 = Resistor [tolerance=±5% resistance=10k package="0603 [SMD]"]
  S1 = Toggle Switch [package=THT]
  VCC1 = 4 x AAA Battery Mount

nets:
  GND: Part1.GND, RE1.EncoderPinC, Part2.GND, PIR1.GND, R1.Pin_1, VCC1.-
  N1: Part1.D2, RE1.EncoderPinA
  N2: Part1.D3, R1.Pin_0
  N3: Part1.D6, Part2.IN
  N4: Part1.D8, RE1.EncoderPinB
  N5: Part1.D9, PIR1.SIG
  N6: Part1.VIN, S1.L1
  VDD: Part1.5V, Part2.VDD, PIR1.VDD
  N7: S1.COM, VCC1.+

custom parts:
  16 NeoPixel Ring: 16 ultra bright smart LED NeoPixels are arranged in a circle with 1.75" (44.5mm) outer diameter. The rings are 'chainable' - connect the output pin of one to the input pin of another. Use only one microcontroller pin to control as many as you can chain together! Each LED is addressable as the driver chip is inside the LED. Each one has ~18mA constant current drive so the color will be very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
